// Logisim project GATES 3.circ as structural Verilog: 1 circuit, main circuit main
module main (
  input  A,
  input  B,
  input  C,
  output Q
);

  wire A_B_out, and_1_out, BC_2_out, BC_out;

  and A_B (A_B_out, A, B);
  or BC (BC_out, B, C);
  and BC_2 (BC_2_out, C, B);
  and and_1 (and_1_out, BC_out, BC_2_out);
  or or_1 (Q, A_B_out, and_1_out);
endmodule
