// Logisim project Problem11.circ as structural Verilog: 1 circuit, main circuit main
module main (
  input  in_1,
  input  in_2,
  input  in_3,
  input  in_4
);

  wire and_1_out, and_2_out, and_3_out, and_4_out, and_5_out, and_6_out, and_7_out, or_1_out, or_2_out;

  and and_1 (and_1_out, in_4, in_2);
  and and_2 (and_2_out, in_4, in_2);
  and and_3 (and_3_out, in_2, in_4);
  and and_4 (and_4_out, in_4, in_2);
  or or_1 (or_1_out, and_1_out, and_2_out);
  or or_2 (or_2_out, and_3_out, and_4_out);
  and and_5 (and_5_out, or_1_out, in_1);
  and and_6 (and_6_out, in_1, in_3);
  and and_7 (and_7_out, in_3, or_2_out);
  // OR_Gate or_3 has open pins: in0=and_5_out, in1=and_6_out, in2=and_7_out, out=open
endmodule
