// Logisim project Problem15.circ as structural Verilog: 1 circuit, main circuit main
module main (
  input  A,
  input  B,
  input  C,
  input  D,
  output X,
  output Y
);

  wire and_1_out, and_2_out, and_3_out, and_4_out, and_5_out, and_6_out, and_7_out, and_8_out, and_9_out,
       and_10_out, and_11_out, and_12_out, and_13_out, and_14_out, not_1_out, not_2_out, not_3_out,
       not_4_out, or_1_out, or_2_out;

  and and_1 (and_1_out, B, C);
  and and_2 (and_2_out, A, C);
  and and_3 (and_3_out, A, B);
  and and_4 (and_4_out, A, B);
  not not_1 (not_1_out, A);
  not not_2 (not_2_out, B);
  not not_3 (not_3_out, C);
  not not_4 (not_4_out, D);
  and and_5 (and_5_out, and_1_out, D);
  and and_6 (and_6_out, and_2_out, D);
  and and_7 (and_7_out, and_3_out, D);
  and and_8 (and_8_out, and_4_out, C);
  and and_9 (and_9_out, not_1_out, not_2_out);
  and and_10 (and_10_out, not_3_out, not_4_out);
  and and_11 (and_11_out, A, B);
  and and_12 (and_12_out, C, D);
  or or_1 (or_1_out, and_5_out, and_6_out);
  or or_2 (or_2_out, and_7_out, and_8_out);
  and and_13 (and_13_out, and_9_out, and_10_out);
  and and_14 (and_14_out, and_11_out, and_12_out);
  or or_3 (X, or_1_out, or_2_out);
  or or_4 (Y, and_13_out, and_14_out);
endmodule
