// Logisim project Problem4.circ as structural Verilog: 1 circuit, main circuit main
module main (
  input  A,
  input  B,
  input  C,
  output Y
);

  wire and_1_out, and_2_out, not_1_out, not_2_out, or_1_out;

  and and_1 (and_1_out, A, B, C);
  not not_1 (not_1_out, B);
  not not_2 (not_2_out, C);
  or or_1 (or_1_out, not_1_out, not_2_out);
  and and_2 (and_2_out, A, or_1_out);
  or or_2 (Y, and_1_out, and_2_out);
endmodule
