// Logisim project Problem6.circ as structural Verilog: 1 circuit, main circuit main
module main (
  input  A,
  input  B,
  input  C,
  output X
);

  wire D___A_B_out, E___A_C_out, F___A_B_C_out;

  and D___A_B (D___A_B_out, A, B);
  and E___A_C (E___A_C_out, A, C);
  and F___A_B_C (F___A_B_C_out, A, B, C);
  or or_1 (X, D___A_B_out, E___A_C_out, F___A_B_C_out);
endmodule
