// Logisim project Problem8.circ as structural Verilog: 1 circuit, main circuit main
module main (
  input  A,
  input  B,
  input  C,
  output X,
  output Y
);

  wire and_1_out, and_2_out, and_3_out;

  ExactlyOne xor_1 (.out(X), .in0(A), .in1(B), .in2(C));
  and and_1 (and_1_out, C, A);
  and and_2 (and_2_out, A, B);
  and and_3 (and_3_out, B, C);
  or or_1 (Y, and_1_out, and_2_out, and_3_out);
endmodule
